# Fritzing sketch Hardware (saved by Fritzing 0.9.3b)
perfboards: 1

parts:
  IC3 = IC, SIP package, 4 pins  # not connected
  IC2 = IC, SIP package, 20 pins
  IC1 = IC, SIP package, 20 pins [chip_label=STM32F103C8T6]  # not connected
  X1 = USB Connectors [package=s4b-ph]  # not connected
  Bauteil1 = FTDI Basic Programmer
  S1 = Pushbutton [package="[THT]"]
  Jumper0 = female pin header, 3 pins [form="♀ (female)"]
  Jumper1 = female pin header, 3 pins [form="♀ (female)"]
  MPU9250_MPU-1 = SparkFun IMU Breakout - MPU-9250 [part_number=" SEN-13762"]
  LED1 = Super Flux LED blue [color=Blue]  # not connected
  LED5 = Super Flux LED blue [color=Red]  # not connected

nets:
  N1: IC2.pin6, Bauteil1.RXI
  N2: IC2.pin7, Bauteil1.TXO
  N3: IC2.pin14, MPU9250_MPU-1.SCL/SCLK
  N4: IC2.pin15, MPU9250_MPU-1.SDA/SDI
  N5: S1.Pin_1, S1.Pin_2
  N6: S1.Pin_3, S1.Pin_4
  N7: Jumper0.pin1, Jumper0.pin2, Jumper0.pin3
  N8: Jumper1.pin2, Jumper1.pin3
